// Logisim project ALUController.circ as structural Verilog: 1 circuit, main circuit main
module main (
  input  [5:0] func,
  output [4:0] map_out
);

  wire a_not, and_1_out, and_2_out, and_3_out, and_4_out, and_5_out, and_6_out, and_7_out, and_8_out,
       and_9_out, and_10_out, and_11_out, and_12_out, and_13_out, and_14_out, and_15_out, and_16_out,
       and_17_out, and_18_out, and_19_out, and_20_out, b_not, c_not, d_not, e_not, f_not, or_2_out, or_3_out,
       or_4_out, or_5_out, or_6_out, or_7_out;

  not not_1 (a_not, func[5]);
  not not_2 (b_not, func[4]);
  not not_3 (c_not, func[3]);
  not not_4 (d_not, func[2]);
  not not_5 (e_not, func[1]);
  not not_6 (f_not, func[0]);
  and and_1 (and_1_out, func[5], func[3]);
  and and_2 (and_2_out, func[2], func[1], func[0]);
  and and_3 (and_3_out, func[2], func[5]);
  and and_4 (and_4_out, func[2], f_not);
  and and_5 (and_5_out, a_not, func[2]);
  and and_6 (and_6_out, func[0], a_not);
  and and_7 (and_7_out, func[5], func[1], c_not, f_not);
  and and_8 (and_8_out, d_not, func[3]);
  and and_9 (and_9_out, c_not, a_not, func[2]);
  and and_10 (and_10_out, func[4], func[1]);
  and and_11 (and_11_out, func[5], d_not, func[0]);
  and and_12 (and_12_out, func[1], b_not, d_not);
  or or_1 (map_out[4], and_1_out, and_2_out);
  or or_2 (or_2_out, f_not, d_not);
  and and_13 (and_13_out, func[5], c_not);
  or or_3 (or_3_out, func[3], and_3_out);
  or or_4 (or_4_out, and_11_out, and_4_out);
  or or_5 (or_5_out, func[4], and_5_out, func[0]);
  or or_6 (or_6_out, func[5], and_12_out);
  or or_7 (or_7_out, and_8_out, and_9_out);
  and and_14 (and_14_out, e_not, func[0]);
  and and_15 (and_15_out, or_2_out, and_13_out);
  and and_16 (and_16_out, e_not, or_3_out);
  and and_17 (and_17_out, or_4_out, func[1]);
  and and_18 (and_18_out, e_not, or_5_out);
  and and_19 (and_19_out, f_not, or_6_out);
  and and_20 (and_20_out, or_7_out, e_not);
  or or_8 (map_out[3], and_10_out, and_14_out, and_15_out);
  or or_9 (map_out[2], and_16_out, and_17_out);
  or or_10 (map_out[1], and_18_out, and_6_out, and_7_out);
  or or_11 (map_out[0], and_19_out, and_20_out);

  // Other names for the same wires on the sheet: f = func[0]; e = func[1]; d = func[2]; c = func[3]; b = func[4];
  //   a = func[5]; M5 = map_out[0]; M4 = map_out[1]; M3 = map_out[2]; M2 = map_out[3]; M1 = map_out[4]
endmodule
