// Logisim project EXMEM.circ as structural Verilog: 1 circuit, main circuit EX_MEM
module EX_MEM (
  input  Clock,
  input  [31:0] ResultIn,
  input  [31:0] AddressCacheIn,
  input  ZeroIn,
  input  BranchIn,
  input  RtypeIn,
  input  JumpIn,
  input  MemToRegIn,
  input  RegDstIn,
  input  RegWrEnIn,
  input  [3:0] MemWriteMaskIn,
  input  LBIn,
  input  [4:0] WrIdxIn,
  input  CAccIn,
  input  Freeze,
  output [31:0] ResultOut,
  output [31:0] AddressCacheOut,
  output ZeroOut,
  output BranchOut,
  output RtypeOut,
  output JumpOut,
  output MemToRegOut,
  output RegDstOut,
  output RegWrEnOut,
  output [3:0] MemWriteMaskOut,
  output LBOut,
  output [4:0] WrIdxOut,
  output CAccOut
);

  wire xor_1_out;

  xor xor_1 (xor_1_out, 1'b1, Freeze);
  Register #(.width(32)) register_1 (.D(ResultIn), .en(xor_1_out), .clk(Clock), .Q(ResultOut));  // open: clr
  Register #(.width(1)) register_2 (.D(ZeroIn), .en(xor_1_out), .clk(Clock), .Q(ZeroOut));  // open: clr
  Register #(.width(1)) register_3 (.D(RtypeIn), .en(xor_1_out), .clk(Clock), .Q(RtypeOut));  // open: clr
  Register #(.width(1)) register_4 (.D(MemToRegIn), .en(xor_1_out), .clk(Clock), .Q(MemToRegOut));  // open: clr
  Register #(.width(1)) register_5 (.D(RegDstIn), .en(xor_1_out), .clk(Clock), .Q(RegDstOut));  // open: clr
  Register #(.width(1)) register_6 (.D(RegWrEnIn), .en(xor_1_out), .clk(Clock), .Q(RegWrEnOut));  // open: clr
  Register #(.width(4)) register_7 (.D(MemWriteMaskIn), .en(xor_1_out), .clk(Clock), .Q(MemWriteMaskOut));  // open: clr
  Register #(.width(1)) register_8 (.D(LBIn), .en(xor_1_out), .clk(Clock), .Q(LBOut));  // open: clr
  Register #(.width(5)) register_9 (.D(WrIdxIn), .en(xor_1_out), .clk(Clock), .Q(WrIdxOut));  // open: clr
  Register #(.width(1)) register_10 (.D(CAccIn), .en(xor_1_out), .clk(Clock), .Q(CAccOut));  // open: clr
  Register #(.width(32)) register_11 (
    .D(AddressCacheIn), .en(xor_1_out), .clk(Clock), .Q(AddressCacheOut));  // open: clr
  Register #(.width(1)) register_12 (.D(BranchIn), .en(xor_1_out), .clk(Clock), .Q(BranchOut));  // open: clr
  Register #(.width(1)) register_13 (.D(JumpIn), .en(xor_1_out), .clk(Clock), .Q(JumpOut));  // open: clr
endmodule
