// Logisim project EX_MEM2.circ as structural Verilog: 1 circuit, main circuit EX_MEM_PC
module EX_MEM_PC (
  input  Clock,
  input  [31:0] J_PCIN,
  input  [31:0] PCIN,
  input  [31:0] BR_PCIN,
  output [31:0] J_PCOUT,
  output [31:0] PCOUT,
  output [31:0] BR_PCOUT
);

  Register #(.width(32)) register_1 (.D(J_PCIN), .clk(Clock), .Q(J_PCOUT));  // open: en, clr
  Register #(.width(32)) register_2 (.D(PCIN), .clk(Clock), .Q(PCOUT));  // open: en, clr
  Register #(.width(32)) register_3 (.D(BR_PCIN), .clk(Clock), .Q(BR_PCOUT));  // open: en, clr
endmodule
