// Logisim project ID_EX2.circ as structural Verilog: 1 circuit, main circuit ID_EX_PC
module ID_EX_PC (
  input  Clock,
  input  [31:0] J_PCIN,
  input  [31:0] PCIn,
  input  reset,
  output [31:0] J_PCOUT,
  output [31:0] PCOut
);

  Register #(.width(32)) register_1 (.D(J_PCIN), .clk(Clock), .Q(J_PCOUT), .clr(reset));  // open: en
  Register #(.width(32)) register_2 (.D(PCIn), .clk(Clock), .Q(PCOut), .clr(reset));  // open: en
endmodule
