// Logisim project MEMDB.circ as structural Verilog: 1 circuit, main circuit MEM_WB
module MEM_WB (
  input  Clock,
  input  [31:0] CacheReadDataIn,
  input  MemToRegIn,
  input  JumpIn,
  input  RegDstIn,
  input  RegWrEnIn,
  input  [31:0] ALU_RES,
  input  [4:0] WrIdxIn,
  input  [31:0] PCIN,
  input  SyscalIN,
  input  JRIN,
  output [31:0] CacheReadOut,
  output MemToRegOut,
  output JumpOut,
  output RegDstOut,
  output RegWrEnOut,
  output [31:0] AluRes_WB,
  output [4:0] WrIdxOut,
  output [31:0] PCOUT,
  output SyscallOut,
  output JROUT
);

  Register #(.width(32)) register_1 (.D(CacheReadDataIn), .clk(Clock), .Q(CacheReadOut));  // open: en, clr
  Register #(.width(1)) register_2 (.D(MemToRegIn), .clk(Clock), .Q(MemToRegOut));  // open: en, clr
  Register #(.width(1)) register_3 (.D(JumpIn), .clk(Clock), .Q(JumpOut));  // open: en, clr
  Register #(.width(1)) register_4 (.D(RegDstIn), .clk(Clock), .Q(RegDstOut));  // open: en, clr
  Register #(.width(1)) register_5 (.D(RegWrEnIn), .clk(Clock), .Q(RegWrEnOut));  // open: en, clr
  Register #(.width(32)) register_6 (.D(ALU_RES), .clk(Clock), .Q(AluRes_WB));  // open: en, clr
  Register #(.width(5)) register_7 (.D(WrIdxIn), .clk(Clock), .Q(WrIdxOut));  // open: en, clr
  Register #(.width(32)) register_8 (.D(PCIN), .clk(Clock), .Q(PCOUT));  // open: en, clr
  Register #(.width(1)) register_9 (.D(SyscalIN), .clk(Clock), .Q(SyscallOut));  // open: en, clr
  Register #(.width(1)) register_10 (.D(JRIN), .clk(Clock), .Q(JROUT));  // open: en, clr
endmodule
