// Logisim project alu.circ as structural Verilog: 1 circuit, main circuit ALU
module ALU (
  input  [31:0] ReadData1,
  input  [31:0] ReadData2,
  input  [4:0] ControlBits,
  output [31:0] Result,
  output Zero
);

  wire comparator_3_lt, comparator_4_eq, comparator_5_eq, comparator_6_eq, comparator_7_eq, comparator_7_lt,
       comparator_8_eq, comparator_9_eq, comparator_10_eq, comparator_10_gt, comparator_11_eq,
       comparator_12_gt, comparator_13_eq, not_1_out, or_2_out, or_3_out, Z5, Z6, Z20, Z21, Z22, Z23, Z24;
  wire [31:0] I0, I1, I2, I3, I4, I7, I8, I9, I10, I11, I12, I13, I14, I15, I16, I17, I18, I25, undriven;

  Comparator #(.width(5)) comparator_1 (.a(ControlBits), .b(5'b00101), .eq(Z5));  // open: gt, lt
  Shifter #(.width(32)) shifter_1 (.in(ReadData2), .\dist (ReadData1[4:0]), .out(I0));
  Shifter #(.shift("lr"), .width(32)) shifter_2 (.in(ReadData2), .\dist (ReadData1[4:0]), .out(I1));
  Shifter #(.shift("ar"), .width(32)) shifter_3 (.in(ReadData2), .\dist (ReadData1[4:0]), .out(I2));
  Shifter #(.width(32)) shifter_4 (.in(ReadData2), .\dist (ReadData1[4:0]), .out(I3));
  Shifter #(.shift("lr"), .width(32)) shifter_5 (.in(ReadData2), .\dist (ReadData1[4:0]), .out(I4));
  Comparator #(.width(5)) comparator_2 (.a(ControlBits), .b(5'b00110), .eq(Z6));  // open: gt, lt
  Multiplier #(.mode("twosComplement"), .width(32)) multiplier_1 (
    .a(ReadData1), .b(ReadData2), .out(I7));  // open: cin, cout
  Divider #(.mode("twosComplement"), .width(32)) divider_1 (
    .a(ReadData1), .b(ReadData2), .out(I8));  // open: upper, rem
  Adder #(.width(32)) adder_1 (.a(ReadData1), .b(ReadData2), .out(I9));  // open: cin, cout
  Adder #(.width(32)) adder_2 (.a(ReadData1), .b(ReadData2), .out(I10));  // open: cin, cout
  Subtractor #(.width(32)) subtractor_1 (.a(ReadData1), .b(ReadData2), .out(I11));  // open: bin, bout
  Subtractor #(.width(32)) subtractor_2 (.a(ReadData1), .b(ReadData2), .out(I12));  // open: bin, bout
  assign I13 = ReadData1 & ReadData2;  // AND_Gate and_1, 32 bits wide
  assign I14 = ReadData1 | ReadData2;  // OR_Gate or_1, 32 bits wide
  assign I15 = ReadData1 ^ ReadData2;  // XOR_Gate xor_1, 32 bits wide
  assign I16 = ~(ReadData1 | ReadData2);  // NOR_Gate nor_1, 32 bits wide
  Comparator #(.width(32)) comparator_3 (.a(ReadData1), .b(ReadData2), .lt(comparator_3_lt));  // open: gt, eq
  Adder #(.width(32)) adder_3 (.a(ReadData1), .b(ReadData2), .out(I18));  // open: cin, cout
  Comparator #(.width(5)) comparator_4 (.a(ControlBits), .b(5'b10100), .eq(comparator_4_eq));  // open: gt, lt
  Comparator #(.width(5)) comparator_5 (.a(ControlBits), .b(5'b10101), .eq(comparator_5_eq));  // open: gt, lt
  Comparator #(.width(5)) comparator_6 (.a(ControlBits), .b(5'b10110), .eq(comparator_6_eq));  // open: gt, lt
  Comparator #(.width(32)) comparator_7 (
    .a(ReadData1), .b({32{1'b0}}), .eq(comparator_7_eq), .lt(comparator_7_lt));  // open: gt
  Comparator #(.width(5)) comparator_8 (.a(ControlBits), .b(5'b10111), .eq(comparator_8_eq));  // open: gt, lt
  Comparator #(.width(5)) comparator_9 (.a(ControlBits), .b(5'b11000), .eq(comparator_9_eq));  // open: gt, lt
  Comparator #(.width(32)) comparator_10 (
    .a(ReadData1), .b({32{1'b0}}), .gt(comparator_10_gt), .eq(comparator_10_eq));  // open: lt
  assign I17 = {{31{1'b0}}, comparator_3_lt};  // Bit_Extender bit_extender_1
  Comparator #(.width(32)) comparator_11 (.a(ReadData1), .b(ReadData2), .eq(comparator_11_eq));  // open: gt, lt
  Comparator #(.width(32)) comparator_12 (.a(ReadData1), .b({32{1'b0}}), .gt(comparator_12_gt));  // open: eq, lt
  Shifter #(.width(32)) shifter_6 (.in(ReadData2), .\dist (5'b10000), .out(I25));
  Comparator #(.width(32)) comparator_13 (.a(ReadData1), .b(ReadData2), .eq(comparator_13_eq));  // open: gt, lt
  not not_1 (not_1_out, comparator_11_eq);
  or or_2 (or_2_out, comparator_7_eq, comparator_7_lt);
  or or_3 (or_3_out, comparator_10_gt, comparator_10_eq);
  and and_2 (Z20, comparator_4_eq, comparator_13_eq);
  and and_3 (Z21, comparator_5_eq, not_1_out);
  and and_4 (Z22, comparator_6_eq, or_2_out);
  and and_5 (Z23, comparator_8_eq, comparator_12_gt);
  and and_6 (Z24, comparator_9_eq, or_3_out);
  Multiplexer #(.enable("true"), .select(5), .width(32)) multiplexer_1 (
    .in0(I0), .in1(I1), .in2(I2), .in3(I3), .in4(I4), .in5(ReadData1), .in6({32{1'b1}}), .in7(I7), .in8(I8),
    .in9(I9), .in10(I10), .in11(I11), .in12(I12), .in13(I13), .in14(I14), .in15(I15), .in16(I16), .in17(I17),
    .in18(I18), .in19(I18), .in25(I25), .in31(undriven), .out(Result), .sel(ControlBits));  // open: in20, in21, in22, in23, in24, in26, in27, in28, in29, in30, en
  Multiplexer #(.select(5)) multiplexer_2 (
    .in0(1'b0), .in1(1'b0), .in2(1'b0), .in3(1'b0), .in4(1'b0), .in5(Z5), .in6(Z6), .in7(1'b0), .in8(1'b0),
    .in9(1'b0), .in10(1'b0), .in11(1'b0), .in12(1'b0), .in13(1'b0), .in14(1'b0), .in15(1'b0), .in16(1'b0),
    .in17(1'b0), .in18(1'b0), .in19(1'b0), .in20(Z20), .in21(Z21), .in22(Z22), .in23(Z23), .in24(Z24),
    .in25(1'b0), .in26(1'b0), .in27(1'b0), .in28(1'b0), .in29(1'b0), .in30(1'b0), .in31(1'b0), .out(Zero),
    .sel(ControlBits));

  // Other names for the same wires on the sheet: I5[31:0] = ReadData1; I19[31:0] = I18

  // Notes on the sheet:
  //   syscall
  //   signed?
  //   unsigned?
endmodule
