// Logisim project branchDetector.circ as structural Verilog: 1 circuit, main circuit branch_detector
module branch_detector (
  input  [5:0] Opcode,
  output Branch,
  output Jump
);

  wire and_1_out, and_2_out, I0_N, I1_N, I2_N, I3_N, I4_N, I5_N;

  and and_1 (and_1_out, Opcode[0], I1_N, I3_N);
  and and_2 (and_2_out, I3_N, Opcode[2]);
  and and_3 (Jump, I5_N, I3_N, I2_N, Opcode[1]);
  or or_1 (Branch, and_1_out, and_2_out);
  not not_1 (I5_N, Opcode[5]);
  not not_2 (I4_N, Opcode[4]);
  not not_3 (I3_N, Opcode[3]);
  not not_4 (I2_N, Opcode[2]);
  not not_5 (I1_N, Opcode[1]);
  not not_6 (I0_N, Opcode[0]);

  // Other names for the same wires on the sheet: I0 = Opcode[0]; I1 = Opcode[1]; I2 = Opcode[2]; I3 = Opcode[3];
  //   I4 = Opcode[4]; I5 = Opcode[5]
endmodule
