// Logisim project branch_predictor.circ as structural Verilog: 1 circuit, main circuit branchPredictor
module branchPredictor (
  input  Jump,
  input  Branch,
  input  Clock,
  input  Zero,
  output Prediction,
  output wrongPrediction,
  output pcBranch,
  output reset
);

  wire and_1_out, and_2_out, and_3_out, and_4_out, and_5_out, and_6_out, comparator_1_gt, counter_1_carry,
       d_ff_1_q, d_ff_3_q, d_ff_5_q, delayedBranch, delayedPrediction, not_1_out, or_1_out, or_2_out, Q1, Q2,
       xor_1_out;

  Counter #(.max('h1), .width(1)) counter_1 (
    .load(1'b0), .up(1'b1), .count(Branch), .clk(Clock), .carry(counter_1_carry));  // open: clr, D, Q
  not not_1 (not_1_out, Q1);
  and and_1 (and_1_out, Q2, Zero);
  and and_2 (and_2_out, Zero, not_1_out);
  or or_1 (or_1_out, and_1_out, and_2_out, and_3_out);
  and and_3 (and_3_out, not_1_out, Q2);
  and and_4 (and_4_out, Q2, Q1);
  and and_5 (and_5_out, Q1, Zero);
  or or_2 (or_2_out, and_4_out, and_5_out, and_6_out);
  and and_6 (and_6_out, Q2, Zero);
  Register #(.width(1)) register_1 (.D(or_1_out), .en(counter_1_carry), .clk(Clock), .Q(Q1));  // open: clr
  Register #(.width(1)) register_2 (.D(or_2_out), .en(counter_1_carry), .clk(Clock), .Q(Q2));  // open: clr
  xor xor_1 (xor_1_out, delayedPrediction, Zero);
  and and_7 (wrongPrediction, delayedBranch, xor_1_out);
  Comparator #(.mode("unsigned"), .width(2)) comparator_1 (
    .a({Q2, Q1}), .b(2'b01), .gt(comparator_1_gt));  // open: eq, lt
  Multiplexer multiplexer_1 (.in0(1'b0), .in1(comparator_1_gt), .out(Prediction), .sel(Branch));
  D_Flip_Flop d_ff_1 (.D(Branch), .clk(Clock), .Q(d_ff_1_q));  // open: Qn, preset, reset
  D_Flip_Flop d_ff_2 (.D(d_ff_1_q), .clk(Clock), .Q(delayedBranch));  // open: Qn, preset, reset
  D_Flip_Flop d_ff_3 (.D(Prediction), .clk(Clock), .Q(d_ff_3_q));  // open: Qn, preset, reset
  D_Flip_Flop d_ff_4 (.D(d_ff_3_q), .clk(Clock), .Q(delayedPrediction));  // open: Qn, preset, reset
  D_Flip_Flop d_ff_5 (.D(wrongPrediction), .clk(Clock), .Q(d_ff_5_q));  // open: Qn, preset, reset
  or or_3 (reset, wrongPrediction, d_ff_5_q);

  assign pcBranch = Zero;
endmodule
