// Logisim project one_clock_delay.circ as structural Verilog: 1 circuit, main circuit oneClockDelay
module oneClockDelay (
  input  [31:0] DataIn,
  input  clk,
  input  reset,
  input  Frz,
  output [31:0] DataOut
);

  wire xor_1_out;

  Register #(.width(32)) register_1 (.D(DataIn), .en(xor_1_out), .clk(clk), .Q(DataOut), .clr(reset));
  xor xor_1 (xor_1_out, Frz, 1'b1);
endmodule
